# Fritzing sketch GridTiePCB (saved by Fritzing 0.7.5b)
breadboards: 1

parts:
  D1 = Rectifier Diode [part_number=1N4001 package="300 mil [THT]"]
  D2 = Rectifier Diode [part_number=1N4001 package="300 mil [THT]"]
  D3 = Rectifier Diode [part_number=1N4001 package="300 mil [THT]"]
  D4 = Rectifier Diode [part_number=1N4001 package="300 mil [THT]"]
  D5 = Rectifier Diode [part_number=1N4001 package="300 mil [THT]"]
  D6 = Rectifier Diode [part_number=1N4001 package="300 mil [THT]"]
  D7 = Rectifier Diode [part_number=1N4001 package="300 mil [THT]"]
  U1 = 555 Timer [package="DIP8 [THT]"]
  U2 = 555 Timer [package="DIP8 [THT]"]
  C1 = Electrolytic Capacitor [capacitance=1µF package="100 mil [THT, electrolytic]"]
  R2 = Resistor [tolerance=±5% resistance=4.4k package=THT]
  R3 = Resistor [tolerance=±5% resistance=4.4k package=THT]
  R4 = Resistor [tolerance=±5% resistance=4.4k package=THT]
  Y1 = Resonator [frequency="16 Mhz" package=THT]
  Y2 = Resonator [frequency="16 Mhz" package=THT]
  R5 = Resistor [tolerance=±5% resistance=220 package=THT]
  R6 = Resistor [tolerance=±5% resistance=220 package=THT]
  D8 = Rectifier Diode [part_number=1N4001 package="300 mil [THT]"]
  Q1 = NPN-Transistor [package="TO92 [THT]"]
  Q3 = NPN-Transistor [package="TO92 [THT]"]
  R7 = Resistor [tolerance=±5% resistance=220 package=THT]
  R8 = Resistor [tolerance=±5% resistance=220 package=THT]
  D11 = Zener Diode [part_number=1N4732A breakdown_voltage=3.6V package="300 mil [THT]"]
  D12 = Zener Diode [part_number=1N4732A breakdown_voltage=3.6V package="300 mil [THT]"]
  Q4 = Basic FET N-Channel [package="TO220 [THT]"]
  Q5 = Basic FET N-Channel [package="TO220 [THT]"]
  D13 = Schottky Diode [part_number=1N5817 package="300 mil [THT]"]
  R9 = Resistor [tolerance=±5% resistance=220 package=THT]
  D14 = Rectifier Diode [part_number=1N4001 package="300 mil [THT]"]
  C2 = Ceramic Capacitor [capacitance=100nF package="200 mil [THT, multilayer]"]
  J3 = screw terminal, 3 pins
  J2 = Screw terminal - 2 pins [package=THT]
  J1 = Screw terminal - 2 pins [package=THT]

nets:
  N1: D1.cathode, D4.anode, J1.pin2
  N2: D1.anode, D2.anode, U1.Ground, U2.Ground, C1.-, Y1.1, Y2.1, Q1.E, Q3.E, Q4.source, Q5.source, C2.1, J3.pin3
  N3: D2.cathode, D3.anode, D12.anode, J1.pin1
  N4: D3.cathode, D4.cathode, D5.anode, D7.anode
  N5: D5.cathode, D6.anode
  N6: D6.cathode, U1.Control_Voltage
  N7: D7.cathode, U1.Reset, U1.Vcc_Supply_Voltage, U2.Reset, U2.Vcc_Supply_Voltage, C1.+, R2.Pin_0, R4.Pin_0, R9.Pin_0
  N8: U1.Trigger, U2.Output
  N9: U1.Output, R5.Pin_0, R6.Pin_0
  N10: U1.Threshold, U1.Discharge, R2.Pin_1, C2.0
  N11: U2.Trigger, U2.Threshold, U2.Discharge, R3.Pin_0, R3.Pin_1, R4.Pin_1, Y1.0
  N12: U2.Control_Voltage, Y2.0
  N13: R5.Pin_1, Q4.gate, D14.anode
  N14: R6.Pin_1, D8.anode, Q5.gate
  N15: D8.cathode, Q3.C
  N16: Q1.B, R8.Pin_0
  N17: Q1.C, R7.Pin_1, R9.Pin_1, D14.cathode
  N18: Q3.B, R7.Pin_0
  N19: R8.Pin_1, D11.anode
  N20: D11.cathode, D12.cathode
  N21: Q4.drain, J2.pin1
  N22: Q5.drain, J2.pin2
  N23: D13.cathode, J3.pin1
  N24: D13.anode, J3.pin2
